// Logisim project mux4to1_test.circ as structural Verilog: 1 circuit, main circuit main
module main (
  output out_1,
  output out_2,
  output out_3,
  output out_4,
  output [1:0] out_5,
  output halt,
  output [3:0] out_7,
  output out_8
);

  wire clock_1_out;
  wire [6:0] adder_1_out;

  Clock clock_1 (.out(clock_1_out));
  Adder #(.width(7)) adder_1 (
    .a(7'b0000001), .b({halt, out_5, out_4, out_3, out_2, out_1}), .out(adder_1_out));  // open: cin, cout
  Register #(.width(7)) register_1 (
    .D(adder_1_out), .clk(clock_1_out), .Q({halt, out_5, out_4, out_3, out_2, out_1}));  // open: en, clr
  // Dec2to4 dec2to4_1: pin names not known; wires that end beside it: out_5, {halt, out_5, out_4, out_3, out_2, out_1}, out_7
  // Mut4to1 mut4to1_1: pin names not known; wires that end beside it: out_1, out_2, out_3, out_4, out_5, out_8

  // Other names for the same wires on the sheet: In_A = out_1; In_B = out_2; In_C = out_3; In_D = out_4;
  //   Sel[1:0] = out_5
endmodule
